// Logisim project ALU.circ as structural Verilog: 1 circuit, main circuit ALU
module ALU (
  input  [31:0] BusB,
  input  [31:0] BusA,
  output out_3,
  output out_4,
  output out_5,
  output [31:0] BusD
);

  wire undriven_3, undriven_4, undriven_5;
  wire [1:0] undriven, undriven_2, undriven_6;
  wire [31:0] arithmeticunit_1_rd, logicunit_1_rd, shifter_1_rt;
  wire [31:1] undriven_7;

  LogicUnit logicunit_1 (.Rs(BusA), .Rt(BusB), .LogicOp(undriven), .Rd(logicunit_1_rd));
  ArithmeticUnit arithmeticunit_1 (.Rs(BusA), .Rs_2(BusB), .Sub(undriven_3), .Rd(arithmeticunit_1_rd));
  Multiplexer #(.select(2), .width(32), .enable("false")) multiplexer_1 (
    .in0(logicunit_1_rd), .in1(arithmeticunit_1_rd), .in2({undriven_7, out_5}), .in3(shifter_1_rt),
    .out(BusD), .sel(undriven_6));
  CompareUnit compareunit_1 (
    .Rs(BusA), .Rt(BusB), .Branch(undriven_4), .Unsigned(undriven_5), .out_5(out_5), .out_6(out_4),
    .out_7(out_3));
  Shifter shifter_1 (.Rs(BusA), .Imm(BusB[4:0]), .ShiftOp(undriven_2), .Rt(shifter_1_rt));
endmodule
